// Logisim project Taller_1.circ as structural Verilog
module ABCML (
  input  A,
  input  B,
  input  C,
  output M,
  output L
);

  wire and_1_out, and_2_out, and_3_out, and_4_out, and_5_out, and_6_out, and_7_out, not_1_out, not_2_out,
       not_3_out, not_4_out;

  and and_1 (and_1_out, B, C);
  and and_2 (and_2_out, A, C);
  and and_3 (and_3_out, A, B);
  not not_1 (not_1_out, A);
  not not_2 (not_2_out, A);
  not not_3 (not_3_out, B);
  not not_4 (not_4_out, C);
  or or_1 (M, and_1_out, and_2_out, and_3_out);
  and and_4 (and_4_out, not_1_out, C);
  and and_5 (and_5_out, not_2_out, B);
  and and_6 (and_6_out, A, not_3_out);
  and and_7 (and_7_out, A, not_4_out);
  or or_2 (L, and_4_out, and_5_out, and_6_out, and_7_out);
endmodule

module ABCDS1S2 (
  input  A,
  input  B,
  input  C,
  input  D,
  output S1,
  output S2
);

  wire and_1_out, and_2_out, and_3_out, and_4_out, and_5_out, and_6_out, and_7_out, and_8_out, and_9_out,
       and_10_out, not_1_out, not_2_out, not_3_out, not_4_out, not_5_out, not_6_out, not_7_out, not_8_out,
       not_9_out, not_10_out, not_11_out, not_12_out;

  and and_1 (and_1_out, B, C, D);
  and and_2 (and_2_out, A, C, D);
  and and_3 (and_3_out, A, B, D);
  and and_4 (and_4_out, A, B, C);
  not not_1 (not_1_out, A);
  not not_2 (not_2_out, B);
  not not_3 (not_3_out, A);
  not not_4 (not_4_out, C);
  not not_5 (not_5_out, A);
  not not_6 (not_6_out, D);
  not not_7 (not_7_out, B);
  not not_8 (not_8_out, C);
  not not_9 (not_9_out, B);
  not not_10 (not_10_out, D);
  not not_11 (not_11_out, C);
  not not_12 (not_12_out, D);
  or or_1 (S1, and_1_out, and_2_out, and_3_out, and_4_out);
  and and_5 (and_5_out, not_1_out, not_2_out, C, D);
  and and_6 (and_6_out, not_3_out, B, not_4_out, D);
  and and_7 (and_7_out, not_5_out, B, C, not_6_out);
  and and_8 (and_8_out, A, not_7_out, not_8_out, D);
  and and_9 (and_9_out, A, not_9_out, C, not_10_out);
  and and_10 (and_10_out, A, B, not_11_out, not_12_out);
  or or_2 (S2, and_5_out, and_6_out, and_7_out, and_8_out, and_9_out, and_10_out);
endmodule

module ABCH (
  input  A,
  input  B,
  input  C,
  output H
);

  wire and_1_out, and_2_out, not_1_out, not_2_out;

  not not_1 (not_1_out, C);
  not not_2 (not_2_out, B);
  and and_1 (and_1_out, B, not_1_out);
  and and_2 (and_2_out, A, not_2_out, C);
  or or_1 (H, and_1_out, and_2_out);
endmodule

module Cajas (
  input  A,
  input  B,
  input  C,
  output M,
  output P
);

  wire and_2_out, and_3_out, and_4_out, not_1_out, not_2_out, not_3_out;

  not not_1 (not_1_out, A);
  not not_2 (not_2_out, A);
  not not_3 (not_3_out, C);
  and and_1 (P, A, B, C);
  and and_2 (and_2_out, not_1_out, C);
  and and_3 (and_3_out, not_2_out, B);
  and and_4 (and_4_out, A, not_3_out);
  or or_1 (M, and_2_out, and_3_out, and_4_out);
endmodule
